# Fritzing sketch TempAndHumidProject (saved by Fritzing 0.9.3b)
breadboards: 1

parts:
  Raspberry_Pi_1 = Raspberry Pi 3 [part_number=RPI-3-V1.2]
  LED1 = LED - 5mm [color="Red (633nm)" package="5 mm [THT]"]
  LED2 = LED - 5mm [color="Green (555nm)" package="5 mm [THT]"]
  R1 = Resistor [tolerance=±5% resistance=220 package=THT]  # not connected
  R2 = Resistor [tolerance=±5% resistance=220 package=THT]  # not connected
  S1 = Pushbutton [package="[THT]"]
  S2 = Pushbutton [package="[THT]"]
  R3 = Resistor [tolerance=±5% resistance=220 package=THT]
  R4 = Resistor [tolerance=±5% resistance=220 package=THT]
  Part1 = LCD1602-I2C
  A1 = DHT22 module

nets:
  N1: Raspberry_Pi_1.3v3, S1.Pin_3, S1.Pin_4, S2.Pin_3, S2.Pin_4
  N2: Raspberry_Pi_1.GPIO2, Part1.SDA
  N3: Raspberry_Pi_1.GPIO3, Part1.SCL
  N4: Raspberry_Pi_1.GIPO4, A1.Out
  GND: Raspberry_Pi_1.GND, R3.Pin_1, R4.Pin_1, Part1.GND, A1.-
  N5: Raspberry_Pi_1.GIPO17, S1.Pin_1, S1.Pin_2, R4.Pin_0
  N6: Raspberry_Pi_1.GIPO27, LED1.anode
  N7: Raspberry_Pi_1.GIPO22, LED2.anode
  N8: Raspberry_Pi_1.GIPO18, S2.Pin_1, S2.Pin_2, R3.Pin_0
  5V: Raspberry_Pi_1.5V, Part1.VCC, A1.+

custom parts:
  LCD1602-I2C: A standard character display, usually with 2x16 characters. Comes in many colors with LCM1602 IIC attached.
  DHT22 module: DHT22 module. Pins VCC Data GND.
